# Fritzing sketch iot_project (saved by Fritzing 0.9.3b)
perfboards: 1

parts:
  ESP8266 = ESP8266 NodeMCU LoLin module
  Battery = LIPO-2000mAh [package=lipo-2000]
  Multiplexer = Analog Digital MUX Breakout
  Potoresistor = Photocell (LDR) [package=THT]
  YL-69 = FC-28 Soil Hygrometer Module
  YL-96_Probe = FC-28 Soil Hygrometer Module - Probe
  Status_LED = LED - 5mm [color="Yellow (595nm)" package="5 mm [THT]"]
  YL-83 = YL-83 Rain Sensor - Control Board
  YL-83_Probe = YL-83 Rain Sensor - Detection Board
  MQ2 = Gas Sensor Breakout Board
  MQ135 = Gas Sensor Breakout Board
  BMP180 = Adafruit BMP180
  DHT1 = DHT11 Humitidy and Temperature Sensor
  DHT11_fc = female pin header, 3 pins [form="♀ (female)"]
  DHT11_mc = male pin header, 3 pins [form="♂ (male)"]
  LED_fc = female pin header, 2 pins [form="♀ (female)"]
  MQ135_fc = female pin header, 3 pins [form="♀ (female)"]
  MQ135_mc = male pin header, 3 pins [form="♂ (male)"]
  MQ2_mc = male pin header, 3 pins [form="♂ (male)"]
  YL69_fc = female pin header, 3 pins [form="♀ (female)"]
  YL69_mc = male pin header, 3 pins [form="♂ (male)"]
  YL83_fc = female pin header, 3 pins [form="♀ (female)"]
  YL83_mc = male pin header, 3 pins [form="♂ (male)"]
  BMP180_fc = female pin header, 4 pins [form="♀ (female)"]
  BMP180_mc = male pin header, 4 pins [form="♂ (male)"]
  Batt_fc = female pin header, 2 pins [form="♀ (female)"]
  Batt_mc = male pin header, 2 pins [form="♂ (male)"]
  LED_mc = male pin header, 2 pins [form="♂ (male)"]
  Photo_fc = female pin header, 3 pins [form="♀ (female)"]
  Photo_mc = male pin header, 3 pins [form="♂ (male)"]
  R2 = Resistor [tolerance=±5% resistance=10k package=THT]
  R3 = Resistor [tolerance=±1% resistance=330 package=THT]
  MQ2_fc = female pin header, 3 pins [form="♀ (female)"]
  R1 = Resistor [tolerance=±5% resistance=4.7k package=THT]
  Reset_btn = Momentary Switch [package=ksa_sealed_tac_switch]
  RST_fc = female pin header, 2 pins [form="♀ (female)"]
  RST_mc = male pin header, 2 pins [form="♂ (male)"]

nets (from the schematic view):
  N1: ESP8266.D0, ESP8266.RST, RST_fc.pin2
  N2: ESP8266.D1, BMP180_fc.pin2
  N3: ESP8266.D2, BMP180_fc.pin3
  N4: ESP8266.D3, Multiplexer.S1
  N5: ESP8266.D4, Multiplexer.S0
  3V3: ESP8266.3V3, Multiplexer.VCC, DHT11_fc.pin1, YL69_fc.pin1, YL83_fc.pin1, BMP180_fc.pin1, Photo_fc.pin1, R1.Pin_1
  GND: ESP8266.GND, Multiplexer.GND, Multiplexer.EN, DHT11_fc.pin3, LED_fc.pin2, MQ135_fc.pin3, YL69_fc.pin3, YL83_fc.pin3, BMP180_fc.pin4, Batt_fc.pin2, Photo_fc.pin3, MQ2_fc.pin3, RST_fc.pin1
  N6: ESP8266.D5, DHT11_fc.pin2, R1.Pin_0
  N7: ESP8266.D6, R3.Pin_0
  N8: ESP8266.D7, Multiplexer.S3
  N9: ESP8266.D8, Multiplexer.S2
  N10: ESP8266.Vin, MQ135_fc.pin1, Batt_fc.pin1, MQ2_fc.pin1
  N11: ESP8266.A0, Multiplexer.SIG
  N12: Battery.+, Batt_mc.pin1
  N13: Battery.-, Batt_mc.pin2
  N14: Multiplexer.C0, MQ135_fc.pin2
  N15: Multiplexer.C1, MQ2_fc.pin2
  N16: Multiplexer.C2, YL69_fc.pin2
  N17: Multiplexer.C3, Photo_fc.pin2
  N18: Multiplexer.C4, YL83_fc.pin2
  N19: Potoresistor.pin_0, Photo_mc.pin2, R2.Pin_0
  N20: Potoresistor.pin_1, Photo_mc.pin1
  N21: YL-69.VCC, YL69_mc.pin1
  N22: YL-69.GND, YL69_mc.pin3
  N23: YL-69.AO, YL69_mc.pin2
  N24: YL-69.POS, YL-96_Probe.POS
  N25: YL-69.NEG, YL-96_Probe.NEG
  N26: Status_LED.cathode, LED_mc.pin2
  N27: Status_LED.anode, LED_mc.pin1
  N28: YL-83.VCC, YL83_mc.pin1
  N29: YL-83.GND, YL83_mc.pin3
  N30: YL-83.AO, YL83_mc.pin2
  N31: YL-83.POS, YL-83_Probe.POS
  N32: YL-83.NEG, YL-83_Probe.NEG
  N33: MQ2.A1, MQ2_mc.pin2
  N34: MQ2.H1, MQ2_mc.pin1
  N35: MQ2.GND, MQ2_mc.pin3
  N36: MQ135.A1, MQ135_mc.pin2
  N37: MQ135.H1, MQ135_mc.pin1
  N38: MQ135.GND, MQ135_mc.pin3
  N39: BMP180.+5V, BMP180_mc.pin1
  N40: BMP180.GND, BMP180_mc.pin4
  N41: BMP180.SCL, BMP180_mc.pin2
  N42: BMP180.SDA, BMP180_mc.pin3
  N43: DHT1.VDD, DHT11_mc.pin1
  N44: DHT1.DATA, DHT11_mc.pin2
  N45: DHT1.GND, DHT11_mc.pin3
  N46: LED_fc.pin1, R3.Pin_1
  N47: Photo_mc.pin3, R2.Pin_1
  N48: Reset_btn.1, RST_mc.pin2
  N49: Reset_btn.3, RST_mc.pin1

custom parts:
  ESP8266 NodeMCU LoLin module: ESP8266 based NodeMCU
  FC-28 Soil Hygrometer Module: The FC-28 is a soil hygrometer module that uses the Texas Instruments LM393 comparator chip to provide an analog measurement of soil humidity. The digital output is high when soil moisture is over a certain threshold, as determined by adjusting the potentiometer.
  FC-28 Soil Hygrometer Module - Probe: The FC-28 is a soil hygrometer module that uses the Texas Instruments LM393 comparator chip to provide an analog measurement of soil humidity.
  YL-83 Rain Sensor - Control Board: The YL-83 is a rain sensor that has more resistance when dry and less resistance when wet. The module runs at 5V.
  YL-83 Rain Sensor - Detection Board: The YL-83 is a rain sensor that has more resistance when dry and less resistance when wet. The module runs at 5V.
  Adafruit BMP180: This precision sensor from Bosch is the best low-cost sensing solution for measuring barometric pressure and temperature. Because pressure changes with altitude you can also use it as an altimeter! The sensor is soldered onto a PCB with a 3.3V regulator, I2C level shifter and pull-up resistors on the I2C pins. The BMP180 is the next-generation of sensors from Bosch, and replaces the BMP085.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
  DHT11 Humitidy and Temperature Sensor: DHT11 Humidity and Temperature Sensor
